// Logisim project lab10B.circ as structural Verilog: 2 circuits, main circuit main
module main (
  input  WriteEnable,
  input  [1:0] ReadRegister1,
  input  [1:0] ReadRegister2,
  input  [1:0] WriteRegister,
  input  [15:0] WriteData,
  input  Clock,
  output [15:0] ReadData1,
  output [15:0] ReadData2
);

  Register_File register_file_1 (
    .ReadRegister1(ReadRegister1), .ReadRegister2(ReadRegister2), .WriteRegister(WriteRegister),
    .WriteData(WriteData), .WriteEnable(WriteEnable), .Clock(Clock), .ReadData1(ReadData1),
    .ReadData2(ReadData2));

  // Notes on the sheet:
  //   of your circuit.
  //   These are the inputs
  //   Do not modify this!
  //   Morgan Noonan men83
  //   These are the outputs
  //   of your circuit.
  //   Do not modify this!
endmodule

module Register_File (
  input  [1:0] ReadRegister1,
  input  [1:0] ReadRegister2,
  input  [1:0] WriteRegister,
  input  [15:0] WriteData,
  input  WriteEnable,
  input  Clock,
  output [15:0] ReadData1,
  output [15:0] ReadData2
);

  wire _0, _1, _2, _3;
  wire [15:0] R0_q, R1_q, R2_q, R3_q;

  Demultiplexer #(.select(2)) demultiplexer_1 (
    .out0(_0), .out1(_1), .out2(_2), .out3(_3), .in(WriteEnable), .sel(WriteRegister));  // open: en
  Register #(.width(16)) R0 (.D(WriteData), .en(_0), .Q(R0_q), .clk(Clock));  // open: clr
  Register #(.width(16)) R1 (.D(WriteData), .en(_1), .Q(R1_q), .clk(Clock));  // open: clr
  Register #(.width(16)) R2 (.D(WriteData), .en(_2), .Q(R2_q), .clk(Clock));  // open: clr
  Register #(.width(16)) R3 (.D(WriteData), .en(_3), .Q(R3_q), .clk(Clock));  // open: clr
  Multiplexer #(.select(2), .width(16)) multiplexer_1 (
    .in0(R0_q), .in1(R1_q), .in2(R2_q), .in3(R3_q), .out(ReadData1), .sel(ReadRegister1));  // open: en
  Multiplexer #(.select(2), .width(16)) multiplexer_2 (
    .in0(R0_q), .in1(R1_q), .in2(R2_q), .in3(R3_q), .out(ReadData2), .sel(ReadRegister2));  // open: en

  // Other names for the same wires on the sheet: RR1[1:0] = ReadRegister1; RR2[1:0] = ReadRegister2;
  //   WR2[1:0] = WriteRegister
endmodule
