// Logisim project lab11A.circ as structural Verilog: 4 circuits, main circuit main
module main (
  output [15:0] Instruction,
  output [7:0] Immediate,
  output Register,
  output [3:0] Opcode,
  output [7:0] RegisterWriteData,
  output [7:0] Register0,
  output [7:0] Register1,
  output [7:0] ALUResult
);

  wire clock_1_out, control_1_select, not_1_out;
  wire [1:0] control_1_aluop;
  wire [7:0] adder_1_out, register_1_q;

  Clock clock_1 (.out(clock_1_out));
  Adder adder_1 (.a(8'h1), .b(register_1_q), .out(adder_1_out));  // open: cin, cout
  Register register_1 (.D(adder_1_out), .en(1'b1), .Q(register_1_q), .clk(clock_1_out));  // open: clr
  ROM #(.dataWidth(16)) rom_1 (.addr(register_1_q), .data(Instruction), .sel(1'b1));
  Fields fields_1 (.in_1(Instruction), .Immediate(Immediate), .register(Register), .Opcode(Opcode));
  not not_1 (not_1_out, Register);
  Control control_1 (.Opcode(Opcode), .ALUOp(control_1_aluop), .Select(control_1_select));
  Register A (.D(RegisterWriteData), .en(not_1_out), .Q(Register0), .clk(clock_1_out));  // open: clr
  Register B (.D(RegisterWriteData), .en(Register), .Q(Register1), .clk(clock_1_out));  // open: clr
  ALU alu_1 (.A(Register0), .B(Register1), .Operation(control_1_aluop), .Result(ALUResult));
  Multiplexer #(.width(8)) multiplexer_1 (
    .in0(ALUResult), .in1(Immediate), .out(RegisterWriteData), .sel(control_1_select));  // open: en

  // Notes on the sheet:
  //   contents of rom_1 (hex, n*v repeats v):
  //   a 803 4800 4000
endmodule

module ALU (
  input  [7:0] A,
  input  [7:0] B,
  input  [1:0] Operation,
  output [7:0] Result
);

  wire [7:0] adder_1_out, nand_1_out, nor_1_out, subtractor_1_out;

  Adder adder_1 (.a(A), .b(B), .out(adder_1_out));  // open: cin, cout
  Subtractor subtractor_1 (.a(A), .b(B), .out(subtractor_1_out));  // open: bin, bout
  assign nand_1_out = ~(A & B);  // NAND_Gate nand_1, 8 bits wide
  assign nor_1_out = ~(A | B);  // NOR_Gate nor_1, 8 bits wide
  Multiplexer #(.select(2), .width(8)) multiplexer_1 (
    .in0(adder_1_out), .in1(subtractor_1_out), .in2(nand_1_out), .in3(nor_1_out), .out(Result),
    .sel(Operation));  // open: en
endmodule

module Fields (
  input  [15:0] in_1,
  output [7:0] Immediate,
  output register,
  output [3:0] Opcode
);


  assign Immediate = in_1[7:0];
  assign Opcode = in_1[15:12];
  assign register = in_1[11];
endmodule

module Control (
  input  [3:0] Opcode,
  output [1:0] ALUOp,
  output Select
);

  wire add, \nand , \nor , sub;

  Decoder #(.select(4)) decoder_1 (
    .out0(Select), .out4(add), .out5(sub), .out8(\nor ), .out9(\nand ), .sel(Opcode));  // open: out1, out2, out3, out6, out7, out10, out11, out12, out13, out14, out15, en
  Priority_Encoder #(.select(2)) priority_encoder_1 (
    .in0(1'b1), .in1(sub), .in2(\nand ), .in3(\nor ), .out(ALUOp));  // open: gs, en_out, en_in

  // Other names for the same wires on the sheet: set = Select
endmodule
