// Logisim project lab11B.circ as structural Verilog: 1 circuit, main circuit main
module main (
  input  clear,
  output sel,
  output ld,
  output [3:0] address,
  output [3:0] data
);

  wire A_1, clock_1_out, d_ff_1_q;
  wire [3:0] counter_1_q, counter_2_q;

  Comparator #(.width(4)) comparator_1 (.a(4'b1111), .b(counter_1_q), .eq(A_1));  // open: gt, lt
  assign address = sel ? counter_1_q : 4'bz;  // Controlled_Buffer controlled_buffer_1
  Counter #(.width(4), .max('hf), .ongoal("stay")) counter_1 (
    .D(4'b0000), .Q(counter_1_q), .clk(clock_1_out), .clr(clear));  // open: load, count, carry
  D_Flip_Flop d_ff_1 (.clk(clock_1_out), .D(A_1), .Q(d_ff_1_q), .en(sel), .reset(clear));  // open: Qn, preset
  not not_1 (sel, d_ff_1_q);
  Clock clock_1 (.out(clock_1_out));
  assign data = sel ? counter_2_q : 4'bz;  // Controlled_Buffer controlled_buffer_2
  RAM #(.addrWidth(4), .dataWidth(4)) ram_1 (
    .addr(address), .data(data), .sel(sel), .clk(clock_1_out), .ld(1'b0), .clr(clear));
  Counter #(.width(4), .max('hf)) counter_2 (
    .Q(counter_2_q), .clk(clock_1_out), .clr(clear));  // open: load, D, count, carry

  assign ld = 1'b0;

  // Other names for the same wires on the sheet: clr = clear

  // Notes on the sheet:
  //   These are the inputs
  //   of your circuit.
  //   Do not modify this!
  //   Morgan Noonan -men83
  //   These are the outputs
  //   of your circuit.
  //   Do not modify this!
endmodule
