// Logisim project lab12C.circ as structural Verilog: 3 circuits, main circuit main
module main (
  input  Bit,
  input  Clock,
  output Output
);

  wire [1:0] next_state_new1, register_1_q;

  Register #(.width(2)) register_1 (.D(next_state_new1), .Q(register_1_q), .clk(Clock));  // open: en, clr
  output_circuit u_output (.s1(register_1_q[0]), .s2(register_1_q[1]), .\output (Output));
  subcircuit next_state (
    .s1(register_1_q[0]), .s0(register_1_q[1]), .\input (Bit), .new1(next_state_new1[0]),
    .new0(next_state_new1[1]));

  // Notes on the sheet:
  //   of your circuit.
  //   These are the inputs
  //   Do not modify this!
  //   Morgan Noonan men83@pitt.edu and Alyssa alh273@pitt.edu
  //   These are the outputs
  //   of your circuit.
  //   Do not modify this!
endmodule

module subcircuit (
  input  s1,
  input  s0,
  input  \input ,
  output new1,
  output new0
);

  wire and_1_out, and_2_out, and_3_out, and_4_out, and_5_out, not_1_p2, not_2_p3, not_3_p4, not_4_p3,
       not_5_p3, not_6_p3;

  // NOT_Gate not_1: pin names not known; wires that end beside it: s1, not_1_p2
  // NOT_Gate not_2: pin names not known; wires that end beside it: s0, s1, not_2_p3
  // NOT_Gate not_3: pin names not known; wires that end beside it: s0, s1, s0, not_3_p4
  // NOT_Gate not_4: pin names not known; wires that end beside it: s1, s0, not_4_p3
  // NOT_Gate not_5: pin names not known; wires that end beside it: s0, \input , not_5_p3
  // NOT_Gate not_6: pin names not known; wires that end beside it: s0, \input , not_6_p3
  and and_1 (and_1_out, not_1_p2, s0, \input );
  and and_2 (and_2_out, s1, not_2_p3);
  and and_3 (and_3_out, not_3_p4, not_4_p3, \input );
  and and_4 (and_4_out, s1, not_5_p3, not_6_p3);
  and and_5 (and_5_out, s1, s0, \input );
  // OR_Gate or_1: pin names not known; wires that end beside it: and_1_out, and_1_out, and_2_out, new1
  or or_2 (new0, and_3_out, and_4_out, and_5_out);
endmodule

module output_circuit (
  input  s1,
  input  s2,
  output \output 
);

  and and_1 (\output , s1, s1, s2, s2);
endmodule
