// Logisim project lab8A.circ as structural Verilog: 1 circuit, main circuit main
module main (
  input  A,
  input  B,
  input  C_in,
  output S,
  output C_out
);

  wire _02_out, _03_p3, _04_out, A1_out, A2_out, A3_out, A4_p3, A5_p3, A6_p3, A7_p3, A8_p3, A9_out, A10_out,
       A11_out, not_1_out, not_2_out, not_3_out;

  // NOT_Gate not_1 has open pins: in=open, out=not_1_out
  // NOT_Gate not_2 has open pins: in=open, out=not_2_out
  // NOT_Gate not_3 has open pins: in=open, out=not_3_out
  and A1 (A1_out, not_1_out, not_2_out);
  and A2 (A2_out, not_1_out, B);
  and A3 (A3_out, A, not_2_out);
  // AND_Gate A4: pin names not known; wires that end beside it: A, B, A4_p3
  // AND_Gate A5: pin names not known; wires that end beside it: A1_out, C_in, A5_p3
  // AND_Gate A6: pin names not known; wires that end beside it: A2_out, not_3_out, A6_p3
  // AND_Gate A7: pin names not known; wires that end beside it: A3_out, not_3_out, A7_p3
  // AND_Gate A8: pin names not known; wires that end beside it: A4_p3, C_in, A8_p3
  and A9 (A9_out, C_in, A);
  and A10 (A10_out, C_in, B);
  and A11 (A11_out, B, A);
  or _05 (C_out, A11_out, _04_out);
  or _04 (_04_out, A10_out, A9_out);
  or _02 (_02_out, A8_p3, A7_p3);
  // OR_Gate _03: pin names not known; wires that end beside it: _02_out, S, _03_p3
  or _01 (_03_p3, A6_p3, A5_p3);

  // Notes on the sheet:
  //   These are the inputs
  //   of your circuit.
  //   Do not modify this!
  //   Put your name and id here: Luis Oliveira - lun8
  //   This circuit is wrong :D
  //   Implement here your adder!
  //   These are the outputs
  //   of your circuit.
  //   Do not modify this!
endmodule
