// Logisim project lab8A_grader.circ as structural Verilog: 1 circuit, main circuit main
module main (
  output A,
  output B,
  output Carry_In,
  output Sum,
  output Carry_Out,
  output halt
);

  wire clock_1_out;
  wire [2:0] counter_1_q;

  Clock clock_1 (.out(clock_1_out));
  Counter #(.width(3), .max('h7)) counter_1 (
    .count(1'b1), .Q(counter_1_q), .carry(halt), .clk(clock_1_out));  // open: load, D, clr
  ROM #(.addrWidth(3), .dataWidth(3)) rom_1 (.addr(counter_1_q), .data({Carry_In, B, A}), .sel(1'b1));
  lab8A_main main_1 (.A(A), .B(B), .C_in(Carry_In), .S(Sum), .C_out(Carry_Out));

  // Other names for the same wires on the sheet: Cin = Carry_In; Cout = Carry_Out; S = Sum

  // Notes on the sheet:
  //   contents of rom_1 (hex, n*v repeats v):
  //   0 1 2 3 4 5 6 7
endmodule
