// Logisim project lab8B.circ as structural Verilog: 1 circuit, main circuit main
module main (
  input  A,
  input  B,
  input  C,
  output Q
);

  wire and_1_out;

  and and_1 (and_1_out, B, C);
  or or_1 (Q, and_1_out, A);

  // Notes on the sheet:
  //   of your circuit.
  //   These are the inputs
  //   Do not modify this!
  //   Put your name and id here: Luis Oliveira - lun8
  //   These are the outputs
  //   of your circuit.
  //   Do not modify this!
endmodule
