// Logisim project lab9A.circ as structural Verilog: 1 circuit, main circuit main
module main (
  input  A_1,
  input  A_0,
  input  B_1,
  input  B_0,
  output Y
);

  wire and_1_out, and_2_out, and_3_out, not_1_p3, not_2_p3, not_3_p2, not_4_p2;

  // NOT_Gate not_1: pin names not known; wires that end beside it: B_1, B_0, not_1_p3
  // NOT_Gate not_2: pin names not known; wires that end beside it: B_1, B_0, not_2_p3
  // NOT_Gate not_3: pin names not known; wires that end beside it: B_1, not_3_p2
  // NOT_Gate not_4: pin names not known; wires that end beside it: B_0, not_4_p2
  and and_1 (and_1_out, not_1_p3, not_2_p3);
  and and_2 (and_2_out, A_1, not_3_p2);
  and and_3 (and_3_out, A_1, not_4_p2);
  or or_1 (Y, and_1_out, and_2_out, and_3_out);

  // Notes on the sheet:
  //   of your circuit.
  //   These are the inputs
  //   Do not modify this!
  //   Place the subcircuit generated by logisim
  //   Put your name and id here: Luis Oliveira - lun8
  //   here, make sure everything is connected
  //   These are the outputs
  //   of your circuit.
  //   Do not modify this!
endmodule
