// Logisim project lab9B.circ as structural Verilog: 2 circuits, main circuit main
module main (
  input  [3:0] Number
);

  wire d0, d1, d2, d3, d4, d5, d6, d7;

  Solution solution (
    .Number_to_display(Number), .Segment_configuration({d7, d6, d5, d4, d3, d2, d1, d0}));  // open: in_2
  _7_Segment_Display u_7_segment_display_1 (.g(d0), .f(d1), .a(d2), .b(d3), .e(d7), .d(d6), .c(d5), .dp(d4));

  // Notes on the sheet:
  //   This is what the autograder looks like
  //   1. Modify the solution subcircuit
  //   2. Make sure the circuit still connects correctly
  //   Change the number
  //   If you need to modify this circuit, your solution will fail!
  //   Display changes
endmodule

module Solution (
  input  [3:0] Number_to_display,
  input  in_2,
  output [7:0] Segment_configuration
);

  wire _0, _1, _2, _3, _4, _5, _6, _7, _8, _9, or_1_out, or_2_out, or_3_out, or_4_out, or_5_out, or_6_out,
       or_7_out, or_8_out, or_9_out, or_10_out, or_11_out, or_12_out, or_13_out, or_14_out, or_15_out,
       or_19_out, or_20_out, or_21_out, or_22_out, or_23_out, or_24_out, or_25_out, or_26_out, or_27_out,
       or_28_out, or_29_out, or_30_out, or_31_out, or_32_out, or_33_out, or_34_out, or_35_out, or_36_out,
       or_40_out, or_41_out, undriven, undriven_2, undriven_3, undriven_4, undriven_5, undriven_6,
       undriven_7, undriven_8, undriven_9, undriven_10, undriven_11, undriven_12, undriven_13, undriven_14;

  Decoder #(.select(4)) decoder_1 (
    .out0(_0), .out1(_1), .out2(_2), .out3(_3), .out4(_4), .out5(_5), .out6(_6), .out7(_7), .out8(_8),
    .out9(_9), .sel(Number_to_display));  // open: out10, out11, out12, out13, out14, out15, en
  or or_1 (or_1_out, _2, or_2_out);
  or or_2 (or_2_out, _3, _4, undriven);
  or or_3 (or_3_out, undriven, _5, _6, undriven_2);
  or or_4 (or_4_out, or_3_out, or_5_out);
  or or_5 (or_5_out, undriven_2, _8, _9);
  or or_6 (or_6_out, _0, or_7_out);
  or or_7 (or_7_out, _4, _5, undriven_3);
  or or_8 (or_8_out, undriven_3, _6, _8);
  or or_9 (or_9_out, or_8_out, _9);
  or or_10 (or_10_out, _0, _2, undriven_4);
  or or_11 (or_11_out, or_10_out, or_12_out);
  or or_12 (or_12_out, undriven_4, _3, _5, undriven_5);
  or or_13 (or_13_out, undriven_5, _6, _7, undriven_6);
  or or_14 (or_14_out, or_13_out, or_15_out);
  or or_15 (or_15_out, undriven_6, _8, _9);
  buf or_16 (Segment_configuration[0], or_1_out);  // OR_Gate
  buf or_17 (Segment_configuration[1], or_6_out);  // OR_Gate
  buf or_18 (Segment_configuration[2], or_11_out);  // OR_Gate
  or or_19 (or_19_out, _0, _1, undriven_7);
  or or_20 (or_20_out, undriven_7, _2, _3, undriven_8);
  or or_21 (or_21_out, undriven_8, _4, _7, undriven_9);
  or or_22 (or_22_out, undriven_9, _8, _9);
  or or_23 (or_23_out, _0, _1, undriven_10);
  or or_24 (or_24_out, undriven_10, _3, _4, undriven_11);
  or or_25 (or_25_out, undriven_11, _5, _6, undriven_12);
  or or_26 (or_26_out, undriven_12, _7, _8);
  or or_27 (or_27_out, _0, _2, undriven_13);
  or or_28 (or_28_out, undriven_13, _3, _5, undriven_14);
  or or_29 (or_29_out, undriven_14, _6, _8);
  or or_30 (or_30_out, or_19_out, or_20_out);
  or or_31 (or_31_out, or_21_out, or_22_out);
  or or_32 (or_32_out, or_23_out, or_24_out);
  or or_33 (or_33_out, or_25_out, or_34_out);
  or or_34 (or_34_out, or_26_out, or_26_out, _9);
  or or_35 (or_35_out, or_27_out, or_28_out);
  or or_36 (or_36_out, or_29_out, _9);
  buf or_37 (Segment_configuration[3], or_30_out);  // OR_Gate
  buf or_38 (Segment_configuration[5], or_32_out);  // OR_Gate
  buf or_39 (Segment_configuration[6], or_35_out);  // OR_Gate
  or or_40 (or_40_out, _2, _6);
  or or_41 (or_41_out, _0, or_40_out);
  or or_42 (Segment_configuration[7], or_41_out, _8);

  assign Segment_configuration[4] = in_2;

  // Other names for the same wires on the sheet: number[3:0] = Number_to_display; d0 = Segment_configuration[0];
  //   segments[7:0] = {Segment_configuration[7:5], in_2, Segment_configuration[3:0]}; d1 = Segment_configuration[1];
  //   d2 = Segment_configuration[2]; d3 = Segment_configuration[3]; d5 = Segment_configuration[5];
  //   d6 = Segment_configuration[6]; d7 = Segment_configuration[7]

  // Notes on the sheet:
  //   These are the inputs
  //   of your circuit.
  //   Do not modify this!
  //   Morgan Noonan-men83
  //   These are the outputs
  //   of your circuit.
  //   Do not modify this!
endmodule
