// Logisim project lab9B_grader.circ as structural Verilog: 1 circuit, main circuit main
module main (
  output d7,
  output d6,
  output d5,
  output d4,
  output d3,
  output d2,
  output d1,
  output d0,
  output halt
);

  wire clock_1_out;
  wire [3:0] counter_1_q, rom_1_data;

  Clock clock_1 (.out(clock_1_out));
  Counter #(.width(4), .max('hf)) counter_1 (
    .count(1'b1), .Q(counter_1_q), .clk(clock_1_out));  // open: load, D, carry, clr
  ROM #(.addrWidth(4), .dataWidth(4)) rom_1 (.addr(counter_1_q), .data(rom_1_data), .sel(1'b1));
  Solution solution_1 (
    .Number_to_display(rom_1_data), .Segment_configuration({d7, d6, d5, d4, d3, d2, d1, d0}));  // open: in_2
  Comparator #(.width(4), .mode("unsigned")) comparator_1 (.a(counter_1_q), .b(4'b1001), .gt(halt));  // open: eq, lt
  _7_Segment_Display u_7_segment_display_1 (.g(d0), .f(d1), .a(d2), .b(d3), .e(d7), .d(d6), .c(d5), .dp(d4));

  // Notes on the sheet:
  //   contents of rom_1 (hex, n*v repeats v):
  //   0 1 2 3 4 5 6 7 8 9 a b c d e f
endmodule
