// Logisim project umips.circ as structural Verilog: 1 circuit, main circuit main
module main (
  output [15:0] Reg0,
  output [15:0] Reg1,
  output [15:0] Reg2,
  output [15:0] Reg3,
  output [15:0] Reg4,
  output [15:0] Reg5,
  output [15:0] Reg6,
  output [15:0] Reg7,
  output [3:0] Output3,
  output [3:0] Output2,
  output [3:0] Output1,
  output [3:0] Output0,
  output halt
);

  wire add, addi, addui, ALUbSrc, and_1_out, and_2_out, and_3_out, and_4_out, bn, bp, branch, bx, bz, clock,
       decoder_1_out0, decoder_1_out1, decoder_1_out2, decoder_1_out4, decoder_1_out5, decoder_1_out6,
       decoder_1_out8, decoder_1_out9, div, GT, j, jal, jr, li, LT, lw, mfhi, mflo, mul, \nand , not_2_out,
       not_4_out, \or , or_1_out, or_4_out, put, sllv, srlv, sub, subop, sw, weReg, Z;
  wire [2:0] func, regDataSrc, rs;
  wire [3:0] opcode;
  wire [7:0] adder_1_out, imm, multiplexer_4_out, multiplexer_5_out, PC;
  wire [15:0] ALUout, bit_extender_1_out, bit_extender_2_out, DataMemOut, DataRA, DataRB, Hi, imm16, Lo,
       main_2_result, multiplexer_1_out, multiplexer_3_out, not_1_p2, not_3_out, PC_1;

  or or_1 (or_1_out, add, addui, addi);
  or or_2 (ALUbSrc, addi, addui);
  Priority_Encoder priority_encoder_1 (
    .in0(1'b1), .in1(\or ), .in2(or_1_out), .in3(sub), .in4(mul), .in5(div), .in6(sllv), .in7(srlv),
    .out(func));  // open: en_in, gs, en_out
  Priority_Encoder priority_encoder_2 (
    .in0(1'b1), .in1(li), .in2(lw), .in3(jal), .in4(mfhi), .in5(mflo), .in6(\nand ), .out(regDataSrc));  // open: in7, en_in, gs, en_out
  or or_3 (weReg, add, addui, mflo, addi, li, \nand , lw, \or , srlv, mfhi, jal, sllv, sub);
  Decoder #(.select(4)) decoder_1 (
    .out0(decoder_1_out0), .out1(decoder_1_out1), .out2(decoder_1_out2), .out3(bp), .out4(decoder_1_out4),
    .out5(decoder_1_out5), .out6(decoder_1_out6), .out7(jr), .out8(decoder_1_out8), .out9(decoder_1_out9),
    .out10(mul), .out11(put), .out12(\or ), .out13(sw), .out14(sllv), .out15(halt), .sel(opcode));  // open: en
  Demultiplexer demultiplexer_1 (.out0(mfhi), .out1(j), .in(decoder_1_out9), .sel(subop));  // open: en
  // NOT_Gate #(.width(16)) not_1: pin names not known; wires that end beside it: ALUout, not_1_p2
  assign bit_extender_1_out = {{8{1'b0}}, imm};  // Bit_Extender bit_extender_1
  assign bit_extender_2_out = {{8{imm[7]}}, imm};  // Bit_Extender bit_extender_2
  Demultiplexer demultiplexer_2 (.out0(add), .out1(addui), .in(decoder_1_out0), .sel(subop));  // open: en
  Demultiplexer demultiplexer_3 (.out0(mflo), .out1(addi), .in(decoder_1_out1), .sel(subop));  // open: en
  Demultiplexer demultiplexer_4 (.out0(sub), .out1(jal), .in(decoder_1_out8), .sel(subop));  // open: en
  Multiplexer #(.select(3), .width(16)) multiplexer_1 (
    .in0(ALUout), .in1(imm16), .in2(DataMemOut), .in3(PC_1), .in4(Hi), .in5(Lo), .in6(not_1_p2),
    .out(multiplexer_1_out), .sel(regDataSrc));  // open: in7, en
  Multiplexer #(.width(16)) multiplexer_2 (
    .in0(bit_extender_1_out), .in1(bit_extender_2_out), .out(imm16), .sel(addi));  // open: en
  Demultiplexer demultiplexer_5 (.out0(div), .out1(li), .in(decoder_1_out2), .sel(subop));  // open: en
  Demultiplexer demultiplexer_6 (.out0(lw), .out1(bx), .in(decoder_1_out5), .sel(subop));  // open: en
  Demultiplexer demultiplexer_7 (.out0(srlv), .out1(bz), .in(decoder_1_out6), .sel(subop));  // open: en
  Demultiplexer demultiplexer_8 (.out0(\nand ), .out1(bn), .in(decoder_1_out4), .sel(subop));  // open: en
  Clock clock_1 (.out(clock));
  RegFile_main main_1 (
    .ReadData0(DataRA), .ReadData1(DataRB), .Reg0(Reg0), .Reg1(Reg1), .Reg2(Reg2), .Reg3(Reg3), .Reg4(Reg4),
    .Reg5(Reg5), .Reg6(Reg6), .Reg7(Reg7), .WriteData0(multiplexer_1_out), .WriteSelect0(rs),
    .ReadSelect0(rs), .ReadSelect1(imm[7:5]), .WE0(weReg), .Clock(clock));
  Multiplexer #(.width(16)) multiplexer_3 (
    .in0(DataRB), .in1(imm16), .out(multiplexer_3_out), .sel(ALUbSrc));  // open: en
  ROM #(.dataWidth(16)) rom_1 (.addr(PC), .data({opcode, rs, imm, subop}), .sel(1'b1));
  Adder adder_1 (.a(PC), .b(8'h1), .out(adder_1_out));  // open: cin, cout
  ALU_main main_2 (
    .ALUOp(func), .A(DataRA), .B(multiplexer_3_out), .Result(main_2_result), .GT(GT), .Zero(Z), .LT(LT),
    .in_4(clock), .HI(Hi), .LO(Lo));
  assign PC_1 = {{8{1'b0}}, adder_1_out};  // Bit_Extender bit_extender_3
  Multiplexer #(.width(8)) multiplexer_4 (.in0(imm), .in1(DataRA[7:0]), .out(multiplexer_4_out), .sel(jr));  // open: en
  Multiplexer #(.width(8)) multiplexer_5 (
    .in0(adder_1_out), .in1(multiplexer_4_out), .out(multiplexer_5_out), .sel(or_4_out));  // open: en
  or or_4 (or_4_out, jr, j, branch, jal);
  Register register_1 (.D(multiplexer_5_out), .en(not_2_out), .Q(PC), .clk(clock));  // open: clr
  not not_2 (not_2_out, halt);
  Multiplexer #(.width(16)) multiplexer_6 (
    .in0(main_2_result), .in1(not_3_out), .out(ALUout), .sel(\nand ));  // open: en
  assign not_3_out = ~main_2_result;  // NOT_Gate not_3, 16 bits wide
  RAM #(.dataWidth(16), .bus("separate")) ram_1 (
    .addr(DataRB[7:0]), .din(DataRA), .data(DataMemOut), .str(sw), .clk(clock), .ld(lw));  // open: sel, clr
  not not_4 (not_4_out, Z);
  Register #(.width(16)) register_2 (
    .D(DataRA), .en(put), .Q({Output3, Output2, Output1, Output0}), .clk(clock));  // open: clr
  and and_1 (and_1_out, bp, GT);
  and and_2 (and_2_out, bn, LT);
  and and_3 (and_3_out, bx, not_4_out);
  and and_4 (and_4_out, bz, Z);
  Hex_Digit_Display hex_digit_display_1 (.value(Output2));  // open: dp
  Hex_Digit_Display hex_digit_display_2 (.value(Output3));  // open: dp
  or or_5 (branch, and_1_out, and_2_out, and_3_out, and_4_out);
  Hex_Digit_Display hex_digit_display_3 (.value(Output1));  // open: dp
  Hex_Digit_Display hex_digit_display_4 (.value(Output0));  // open: dp

  // Other names for the same wires on the sheet: rt[2:0] = imm[7:5]

  // Notes on the sheet:
  //   May need to restart Logisim
  //   If you change them in there, changes will be reflected here!
  //   There circuits are in the other 2 files I gave you... I've imported them to this file
  //   You must connect Reg0..7 to the top ports of the register file.
  //   ROM
  //    Don't add/modify/delete any of the input/output pins in this file!
  //   Include everything here (ALU, RegFile, Control, PC, RAM, ROM, LEDs, Displays, ...)
  //   PC
  //   Connect Output3..0 to your LED display.
  //   Output3 is the most significant
  //   RAM
  //   Connect halt to your halt LED
endmodule
