// Logisim project ALU.circ as structural Verilog: 2 circuits, main circuit main
module main (
  input  [2:0] ALUOp,
  input  [15:0] A,
  input  [15:0] B,
  input  in_4,
  output [15:0] Result,
  output [15:0] HI,
  output [15:0] LO,
  output GT,
  output Zero,
  output LT
);

  wire [15:0] adder_1_out, divider_1_out, HiT, LoT, multiplier_1_out, nand_1_out, or_1_out, shifter_1_out,
       shifter_2_out, subtractor_1_out, undriven;

  assign nand_1_out = ~(A & B & undriven);  // NAND_Gate nand_1, 16 bits wide
  assign or_1_out = undriven | A | B;  // OR_Gate or_1, 16 bits wide
  Adder #(.width(16)) adder_1 (.a(A), .b(B), .out(adder_1_out));  // open: cin, cout
  Subtractor #(.width(16)) subtractor_1 (.a(A), .b(B), .out(subtractor_1_out));  // open: bin, bout
  Multiplier #(.width(16)) multiplier_1 (.a(A), .b(B), .out(multiplier_1_out), .cin(HiT), .cout(LoT));
  Divider #(.width(16)) divider_1 (.a(A), .b(B), .out(divider_1_out), .upper(LoT), .rem(HiT));
  Shifter #(.width(16)) shifter_1 (.in(A), .\dist (B[3:0]), .out(shifter_1_out));
  Shifter #(.width(16), .shift("lr")) shifter_2 (.in(A), .\dist (B[3:0]), .out(shifter_2_out));
  Multiplexer #(.select(3), .width(16)) multiplexer_1 (
    .in0(nand_1_out), .in1(or_1_out), .in2(adder_1_out), .in3(subtractor_1_out), .in4(multiplier_1_out),
    .in5(divider_1_out), .in6(shifter_1_out), .in7(shifter_2_out), .out(Result), .sel(ALUOp));  // open: en
  Register #(.width(16)) register_1 (.D(LoT), .Q(LO), .clk(in_4));  // open: en, clr
  Register #(.width(16)) register_2 (.D(HiT), .Q(HI), .clk(in_4));  // open: en, clr
  Comparator #(.width(16)) comparator_1 (.a(A), .b({16{1'b0}}), .gt(GT));  // open: eq, lt
  Comparator #(.width(16)) comparator_2 (.a(A), .b({16{1'b0}}), .eq(Zero));  // open: gt, lt
  Comparator #(.width(16)) comparator_3 (.a(A), .b({16{1'b0}}), .lt(LT));  // open: gt, eq

  // Other names for the same wires on the sheet: Clock = in_4

  // Notes on the sheet:
  //   Inputs
  //    Don't add/modify/delete any of the input/output pins in this file!
  //   Design your ALU in this file
  //   A - First ALU input
  //   B - Second ALU input
  //   Result - ALU main result
  //   Outputs
  //   GT/Zero/LT - Comparison of input A with zero
  //   ALUOp - The control signal defining the behaviour of the ALU
  //   HI/LO the value of the ALU registers using for mul/div
endmodule

module test (
  input  [2:0] in_1,
  input  [15:0] in_2,
  input  [15:0] in_3
);

  wire button_1_out, main_1_gt, main_1_lt, main_1_zero;
  wire [15:0] main_1_hi, main_1_lo, main_1_result;

  main main_1 (
    .ALUOp(in_1), .A(in_2), .B(in_3), .Result(main_1_result), .GT(main_1_gt), .Zero(main_1_zero),
    .LT(main_1_lt), .in_4(button_1_out), .HI(main_1_hi), .LO(main_1_lo));
  Button button_1 (.out(button_1_out));
  // Probe on main_1_result
  // Probe on main_1_hi
  // Probe on main_1_lo
  // Probe on main_1_gt
  // Probe on main_1_zero
  // Probe on main_1_lt

  // Notes on the sheet:
  //   Test your circuit!
endmodule
