// Logisim project umips.circ as structural Verilog: 1 circuit, main circuit main
module main (
  output [15:0] Reg0,
  output [15:0] Reg1,
  output [15:0] Reg2,
  output [15:0] Reg3,
  output [15:0] Reg4,
  output [15:0] Reg5,
  output [15:0] Reg6,
  output [15:0] Reg7,
  output [3:0] Output3,
  output [3:0] Output2,
  output [3:0] Output1,
  output [3:0] Output0,
  output halt
);

  // RegFile_main main_1: pin names not known
  // ALU_main main_2: pin names not known

  // Notes on the sheet:
  //   May need to restart Logisim
  //   Design your CPU in this file
  //   If you change them in there, changes will be reflected here!
  //   You must connect Reg0..7 to the top ports of the register file.
  //   There circuits are in the other 2 files I gave you... I've imported them to this file
  //    Don't add/modify/delete any of the input/output pins in this file!
  //   Include everything here (ALU, RegFile, Control, PC, RAM, ROM, LEDs, Displays, ...)
  //   Connect Output3..0 to your LED display.
  //   Output3 is the most significant
  //   Connect halt to your halt LED
endmodule
